# Fritzing sketch smoothie-on-a-breadboard (saved by Fritzing 0.6.4b)
breadboards: 2

parts:
  LPCXpresso1 = mbed
  CONN1 = USB connector [package=THT]
  DRV1 = A4983
  DRV2 = A4983
  J1 = Screw terminal - 2 pins [package=THT]
  J2 = Screw terminal - 2 pins [package=THT]
  S1 = Pushbutton [package=THT]
  S2 = Pushbutton [package=THT]
  Composants1 = JeePlug experimenter's board
  DRV3 = A4983
  DRV4 = A4983
  R1 = Resistor [tolerance=±5% resistance=10k package=THT]
  R2 = Resistor [tolerance=±5% resistance=10k package=THT]
  R3 = Resistor [tolerance=±5% resistance=10k package=THT]  # not connected
  R4 = Resistor [tolerance=±5% resistance=10k package=THT]
  J3 = Screw terminal - 2 pins [package=THT]
  J4 = Screw terminal - 2 pins [package=THT]
  J5 = Screw terminal - 2 pins [package=THT]
  J6 = Screw terminal - 2 pins [package=THT]
  J7 = Screw terminal - 2 pins [package=THT]
  J8 = Screw terminal - 2 pins [package=THT]
  R5 = Resistor [tolerance=±5% resistance=1k package=THT]
  LED1 = LED - 3mm [color="Red (633nm)" package="3 mm [THT]"]
  J9 = Screw terminal - 2 pins [package=THT]
  Composants2 = JeePlug experimenter's board
  C1 = Electrolytic Capacitor [capacitance=10µF voltage=35V package="100 mil [THT, electrolytic]"]
  R6 = Resistor [tolerance=±5% resistance=4.7k package=THT]
  J10 = Screw terminal - 2 pins [package=THT]
  Q1 = Basic FET P-Channel [package="TO220 [THT]"]
  M1 = Stepper Motor - Bipolar
  M2 = Stepper Motor - Bipolar
  M3 = Stepper Motor - Bipolar
  M5 = Stepper Motor - Bipolar
  R7 = Resistor [tolerance=±5% resistance=220 package=THT]
  R8 = Resistor [tolerance=±5% resistance=10k package=THT]
  J11 = Screw terminal - 2 pins [package=THT]
  J12 = Screw terminal - 2 pins [package=THT]

nets:
  N1: LPCXpresso1.connector0, CONN1.GND, CONN1.chassis5, CONN1.chassis6, S1.leg0, Composants1.A5, LED1.cathode, Composants2.A5, C1.-, J10.pin2
  N2: LPCXpresso1.connector1, CONN1.5V, Composants2.A6
  N3: LPCXpresso1.connector3, S1.leg1
  N4: LPCXpresso1.connector4, Composants1.A1
  N5: LPCXpresso1.connector5, Composants1.A2
  N6: LPCXpresso1.connector6, Composants1.A3
  N7: LPCXpresso1.connector7, Composants1.A4
  N8: LPCXpresso1.connector20, C1.+, R6.Pin_0, J10.pin1
  N9: LPCXpresso1.connector21, Composants2.A3
  N10: LPCXpresso1.connector22, Composants2.A4
  N11: LPCXpresso1.connector24, DRV3.connector7
  N12: LPCXpresso1.connector25, DRV3.connector6
  N13: LPCXpresso1.connector26, DRV4.connector7
  N14: LPCXpresso1.connector27, DRV4.connector6
  N15: LPCXpresso1.connector28, LPCXpresso1.connector51, DRV1.connector14, DRV1.connector15, DRV2.connector14, DRV2.connector15, S2.leg0, Composants1.A6, DRV3.connector14, DRV3.connector15, DRV4.connector14, DRV4.connector15, R1.Pin_0, R2.Pin_0, R4.Pin_0, R5.Pin_1, R6.Pin_1, R8.Pin_0
  N16: LPCXpresso1.connector33, CONN1.d-
  N17: LPCXpresso1.connector34, CONN1.d+
  N18: LPCXpresso1.connector42, R7.Pin_0
  N19: LPCXpresso1.connector46, DRV2.connector7
  N20: LPCXpresso1.connector47, DRV2.connector6
  N21: LPCXpresso1.connector48, S2.leg1
  N22: LPCXpresso1.connector49, DRV1.connector7
  N23: LPCXpresso1.connector50, DRV1.connector6
  N24: DRV1.connector1, DRV1.connector2, DRV1.connector3
  N25: DRV1.connector4, DRV1.connector5
  N26: DRV1.connector8, DRV2.connector8, DRV3.connector8, DRV4.connector8, J9.pin2
  N27: DRV1.connector9, DRV2.connector9, DRV3.connector9, DRV4.connector9, J9.pin1
  N28: DRV1.connector10, J1.pin2, M2.A
  N29: DRV1.connector11, J1.pin1, M2.C
  N30: DRV1.connector12, J2.pin2, M2.B
  N31: DRV1.connector13, J2.pin1, M2.D
  N32: DRV2.connector1, DRV2.connector2, DRV2.connector3, R1.Pin_1
  N33: DRV2.connector4, DRV2.connector5
  N34: DRV2.connector10, J3.pin2, M1.A
  N35: DRV2.connector11, J3.pin1, M1.C
  N36: DRV2.connector12, J4.pin2, M1.B
  N37: DRV2.connector13, J4.pin1, M1.D
  N38: DRV3.connector1, DRV3.connector2
  N39: DRV3.connector3, DRV3.connector4, DRV3.connector5, R4.Pin_1
  N40: DRV3.connector10, J6.pin2, M5.A
  N41: DRV3.connector11, J6.pin1, M5.C
  N42: DRV3.connector12, J5.pin2, M5.B
  N43: DRV3.connector13, J5.pin1, M5.D
  N44: DRV4.connector1, DRV4.connector2
  N45: DRV4.connector3, DRV4.connector4, DRV4.connector5, R2.Pin_1
  N46: DRV4.connector10, J8.pin2, M3.A
  N47: DRV4.connector11, J8.pin1, M3.C
  N48: DRV4.connector12, J7.pin2, M3.B
  N49: DRV4.connector13, J7.pin1, M3.D
  N50: R5.Pin_0, LED1.anode
  N51: Q1.gate, R7.Pin_1, R8.Pin_1
  N52: Q1.drain, J12.pin2
  N53: Q1.source, J11.pin2
  N54: J11.pin1, J12.pin1

notes:
  micro-SD
  breakout
  USB-Serial cable
  thermistor
  stepper drivers
  hotend heater
  USB to host
  steppers Vin
